// Logisim project cpu.circ as structural Verilog: 4 circuits, main circuit CPU
module CPU (
  output [47:0] cpu_out,
  output halt
);

  wire alu_1_negative, alu_1_overflow, alu_1_zero, and_1_out, and_2_out, and_3_out, and_4_out, clk_out,
       comparator_1_eq, comparator_3_eq, comparator_4_eq, comparator_5_eq, decoder_1_out0, decoder_1_out1,
       decoder_1_out2, decoder_1_out3, decoder_1_out4, multiplexer_2_out, multiplexer_7_out, not_1_out,
       not_2_out, not_3_out, or_1_out, or_2_out, or_3_out, reset_out, xor_1_out;
  wire [2:0] adder_1_out, multiplexer_1_out, multiplexer_6_out, register_1_q;
  wire [15:0] adder_2_out, alu_1_c, bit_extender_1_out, bit_extender_2_out, InsMem_data, multiplexer_3_out,
       multiplexer_4_out, multiplexer_5_out, Ra_q, ram_1_dout, Rb_q, Rd_q, registerfile_1_a,
       registerfile_1_b, Rw_q;

  Clock clk (.out(clk_out));
  Button reset (.out(reset_out));
  Register #(.width(3)) register_1 (.D(adder_1_out), .en(1'b1), .clk(clk_out), .Q(register_1_q), .clr(or_1_out));
  or or_1 (or_1_out, reset_out, and_2_out, comparator_1_eq);
  Multiplexer #(.width(3)) multiplexer_1 (
    .in0(cpu_out[18:16]), .in1(cpu_out[25:23]), .out(multiplexer_1_out), .sel(comparator_3_eq));
  or or_2 (or_2_out, decoder_1_out0, and_1_out);
  Adder #(.width(3)) adder_1 (.a(register_1_q), .b(3'b001), .out(adder_1_out));  // open: cin, cout
  Comparator #(.width(3)) comparator_1 (.a(register_1_q), .b(3'b101), .eq(comparator_1_eq));  // open: gt, lt
  Register #(.width(16)) PC (.D(adder_2_out), .en(or_2_out), .clk(clk_out), .Q(cpu_out[47:32]), .clr(reset_out));
  and and_1 (and_1_out, decoder_1_out2, and_3_out);
  Multiplexer multiplexer_2 (.in0(decoder_1_out4), .in1(1'b0), .out(multiplexer_2_out), .sel(cpu_out[30]));
  Adder #(.width(16)) adder_2 (.a(cpu_out[47:32]), .b(multiplexer_3_out), .out(adder_2_out));  // open: cin, cout
  and and_2 (and_2_out, decoder_1_out3, and_3_out);
  Decoder #(.enable("false"), .select(3)) decoder_1 (
    .out0(decoder_1_out0), .out1(decoder_1_out1), .out2(decoder_1_out2), .out3(decoder_1_out3),
    .out4(decoder_1_out4), .sel(register_1_q));  // open: out5, out6, out7
  ROM #(.addrWidth(16), .dataWidth(16)) InsMem (.addr(cpu_out[47:32]), .data(InsMem_data));
  RegisterFile registerfile_1 (
    .Addr_A(cpu_out[22:20]), .Addr_B(multiplexer_1_out), .Addr_C(cpu_out[25:23]), .we(multiplexer_2_out),
    .clk(clk_out), .reset(reset_out), .C(Rw_q), .A(registerfile_1_a), .B(registerfile_1_b));
  Register #(.width(16)) Ra (.D(registerfile_1_a), .en(decoder_1_out1), .clk(clk_out), .Q(Ra_q), .clr(reset_out));
  Register #(.width(16)) Rb (.D(registerfile_1_b), .en(decoder_1_out1), .clk(clk_out), .Q(Rb_q), .clr(reset_out));
  assign bit_extender_1_out = {{13{cpu_out[25]}}, cpu_out[25:23]};  // Bit_Extender bit_extender_1
  Multiplexer #(.width(16)) multiplexer_3 (
    .in0(16'h1), .in1(bit_extender_1_out), .out(multiplexer_3_out), .sel(and_1_out));
  and and_3 (and_3_out, multiplexer_7_out, comparator_5_eq);
  Multiplexer #(.width(16)) multiplexer_4 (
    .in0(Rb_q), .in1(bit_extender_2_out), .out(multiplexer_4_out), .sel(cpu_out[26]));
  Register #(.width(16)) IR (.D(InsMem_data), .en(decoder_1_out0), .clk(clk_out), .Q(cpu_out[31:16]), .clr(reset_out));
  Comparator #(.width(16)) comparator_2 (.a(cpu_out[31:16]), .b(16'h4380), .eq(halt));  // open: gt, lt
  RAM #(.addrWidth(16), .dataWidth(16), .enables("line")) ram_1 (
    .addr(cpu_out[15:0]), .we(and_4_out), .clk(clk_out), .din(Rd_q), .dout(ram_1_dout));
  Register #(.width(16)) Rz (.D(alu_1_c), .en(decoder_1_out2), .clk(clk_out), .Q(cpu_out[15:0]), .clr(reset_out));
  ALU alu_1 (
    .A(Ra_q), .B(multiplexer_4_out), .fun(multiplexer_6_out), .negative(alu_1_negative), .zero(alu_1_zero),
    .overflow(alu_1_overflow), .C(alu_1_c));  // open: carry
  Register #(.width(16)) Rd (.D(Rb_q), .en(decoder_1_out2), .clk(clk_out), .Q(Rd_q), .clr(reset_out));
  Comparator #(.width(2)) comparator_3 (.a(cpu_out[31:30]), .b(2'b11), .eq(comparator_3_eq));  // open: gt, lt
  and and_4 (and_4_out, comparator_3_eq, decoder_1_out3);
  assign bit_extender_2_out = {{12{cpu_out[19]}}, cpu_out[19:16]};  // Bit_Extender bit_extender_2
  Multiplexer #(.width(16)) multiplexer_5 (
    .in0(cpu_out[15:0]), .in1(ram_1_dout), .out(multiplexer_5_out), .sel(comparator_4_eq));
  Comparator #(.width(2)) comparator_4 (.a(cpu_out[31:30]), .b(2'b10), .eq(comparator_4_eq));  // open: gt, lt
  Register #(.width(16)) Rw (.D(multiplexer_5_out), .en(decoder_1_out3), .clk(clk_out), .Q(Rw_q), .clr(reset_out));
  Comparator #(.width(2)) comparator_5 (.a(cpu_out[31:30]), .b(2'b01), .eq(comparator_5_eq));  // open: gt, lt
  Multiplexer #(.width(3)) multiplexer_6 (
    .in0(cpu_out[29:27]), .in1(3'b001), .out(multiplexer_6_out), .sel(comparator_5_eq));
  not not_1 (not_1_out, alu_1_zero);
  xor xor_1 (xor_1_out, alu_1_overflow, alu_1_negative);
  or or_3 (or_3_out, alu_1_zero, xor_1_out);
  not not_2 (not_2_out, xor_1_out);
  not not_3 (not_3_out, or_3_out);
  Multiplexer #(.select(3)) multiplexer_7 (
    .in0(alu_1_zero), .in1(not_1_out), .in2(xor_1_out), .in3(or_3_out), .in4(not_3_out), .in5(not_2_out),
    .out(multiplexer_7_out), .sel(cpu_out[29:27]));  // open: in6, in7

  // Notes on the sheet:
  //   contents of InsMem (hex, n*v repeats v):
  //   493 6d90 2091 491 401 52d 6da0 2122 521 401 15b0 16d0 1621 4540 4e50 1b1 2c91 4e50 3521 2d2 4e50
  //   4d01 21b3 5b1 5b0 4380
endmodule

module ALU (
  input  [2:0] fun,
  input  [15:0] A,
  input  [15:0] B,
  output [15:0] C,
  output negative,
  output carry,
  output overflow,
  output zero
);

  wire xnor_1_out, xor_2_out;
  wire [15:0] adder_1_out, and_1_out, multiplexer_1_out, nor_2_out, or_1_out, shifter_1_out, shifter_2_out,
       shifter_3_out, xor_1_out;

  assign xor_1_out = {16{1'b1}} ^ B;  // XOR_Gate xor_1, 16 bits wide
  xnor xnor_1 (xnor_1_out, multiplexer_1_out[15], A[15]);
  Multiplexer #(.width(16)) multiplexer_1 (.in0(B), .in1(xor_1_out), .out(multiplexer_1_out), .sel(fun[0]));
  nor nor_1 (zero, C[15], C[14], C[13], C[12], C[11], C[10], C[9], C[8], C[7], C[6], C[5], C[4], C[3], C[2], C[1], C[0]);
  Adder #(.width(16)) adder_1 (.a(A), .b(multiplexer_1_out), .out(adder_1_out), .cin(fun[0]), .cout(carry));
  assign and_1_out = A & B;  // AND_Gate and_1, 16 bits wide
  assign or_1_out = A | B;  // OR_Gate or_1, 16 bits wide
  assign nor_2_out = ~(A | B);  // NOR_Gate nor_2, 16 bits wide
  Shifter #(.width(16)) shifter_1 (.in(A), .\dist (B[3:0]), .out(shifter_1_out));
  Shifter #(.shift("lr"), .width(16)) shifter_2 (.in(A), .\dist (B[3:0]), .out(shifter_2_out));
  Shifter #(.shift("ar"), .width(16)) shifter_3 (.in(A), .\dist (B[3:0]), .out(shifter_3_out));
  and and_2 (overflow, xnor_1_out, xor_2_out);
  Multiplexer #(.select(3), .width(16)) multiplexer_2 (
    .in0(adder_1_out), .in1(adder_1_out), .in2(and_1_out), .in3(or_1_out), .in4(nor_2_out),
    .in5(shifter_1_out), .in6(shifter_2_out), .in7(shifter_3_out), .out(C), .sel(fun));
  xor xor_2 (xor_2_out, A[15], C[15]);

  assign negative = C[15];
endmodule

module RegisterFile (
  input  [2:0] Addr_A,
  input  [2:0] Addr_B,
  input  [2:0] Addr_C,
  input  we,
  input  clk,
  input  reset,
  input  [15:0] C,
  output [15:0] A,
  output [15:0] B
);

  wire and_1_out, and_2_out, and_3_out, and_4_out, and_5_out, and_6_out, and_7_out, and_8_out,
       decoder_1_out0, decoder_1_out1, decoder_1_out2, decoder_1_out3, decoder_1_out4, decoder_1_out5,
       decoder_1_out6, decoder_1_out7;
  wire [15:0] R0_q, R1_q, R2_q, R3_q, R4_q, R5_q, R6_q, R7_q;

  Decoder #(.enable("false"), .select(3)) decoder_1 (
    .out0(decoder_1_out0), .out1(decoder_1_out1), .out2(decoder_1_out2), .out3(decoder_1_out3),
    .out4(decoder_1_out4), .out5(decoder_1_out5), .out6(decoder_1_out6), .out7(decoder_1_out7), .sel(Addr_C));
  and and_1 (and_1_out, decoder_1_out6, we);
  and and_2 (and_2_out, decoder_1_out7, we);
  and and_3 (and_3_out, decoder_1_out0, we);
  and and_4 (and_4_out, decoder_1_out1, we);
  and and_5 (and_5_out, decoder_1_out2, we);
  and and_6 (and_6_out, decoder_1_out3, we);
  and and_7 (and_7_out, decoder_1_out4, we);
  and and_8 (and_8_out, decoder_1_out5, we);
  Register #(.width(16)) R0 (.D(C), .en(and_3_out), .clk(clk), .Q(R0_q), .clr(reset));
  Register #(.width(16)) R1 (.D(C), .en(and_4_out), .clk(clk), .Q(R1_q), .clr(reset));
  Register #(.width(16)) R2 (.D(C), .en(and_5_out), .clk(clk), .Q(R2_q), .clr(reset));
  Register #(.width(16)) R3 (.D(C), .en(and_6_out), .clk(clk), .Q(R3_q), .clr(reset));
  Register #(.width(16)) R4 (.D(C), .en(and_7_out), .clk(clk), .Q(R4_q), .clr(reset));
  Register #(.width(16)) R5 (.D(C), .en(and_8_out), .clk(clk), .Q(R5_q), .clr(reset));
  Register #(.width(16)) R6 (.D(C), .en(and_1_out), .clk(clk), .Q(R6_q), .clr(reset));
  Register #(.width(16)) R7 (.D(C), .en(and_2_out), .clk(clk), .Q(R7_q), .clr(reset));
  Multiplexer #(.select(3), .width(16)) multiplexer_1 (
    .in0(R0_q), .in1(R1_q), .in2(R2_q), .in3(R3_q), .in4(R4_q), .in5(R5_q), .in6(R6_q), .in7(R7_q), .out(A),
    .sel(Addr_A));
  Multiplexer #(.select(3), .width(16)) multiplexer_2 (
    .in0(R0_q), .in1(R1_q), .in2(R2_q), .in3(R3_q), .in4(R4_q), .in5(R5_q), .in6(R6_q), .in7(R7_q), .out(B),
    .sel(Addr_B));
endmodule

module RegisterFileTester (
  output halt,
  output [15:0] A,
  output [15:0] B,
  output clk
);

  wire undriven;
  wire [2:0] Addr_A_data, Addr_B_data, Addr_C_data;
  wire [3:0] adder_1_out, addr_q;
  wire [15:0] C_data;

  Clock clock_1 (.out(clk));
  ROM #(.addrWidth(4), .dataWidth(3)) Addr_A (.addr(addr_q), .data(Addr_A_data));
  ROM #(.addrWidth(4), .dataWidth(3)) Addr_B (.addr(addr_q), .data(Addr_B_data));
  ROM #(.addrWidth(4), .dataWidth(3)) Addr_C (.addr(addr_q), .data(Addr_C_data));
  ROM #(.addrWidth(4), .dataWidth(1)) we (.addr(addr_q));  // open: data
  ROM #(.addrWidth(4), .dataWidth(16)) C (.addr(addr_q), .data(C_data));
  Adder #(.width(4)) adder_1 (.a(addr_q), .b(4'b0001), .out(adder_1_out), .cin(1'b0));  // open: cout
  Register #(.width(4)) addr (.D(adder_1_out), .en(1'b1), .clk(clk), .Q(addr_q), .clr(1'b0));
  Comparator #(.width(4)) comparator_1 (.a(addr_q), .b(4'b1111), .eq(halt));  // open: gt, lt
  RegisterFile registerfile_1 (
    .Addr_A(Addr_A_data), .Addr_B(Addr_B_data), .Addr_C(Addr_C_data), .we(undriven), .clk(clk), .reset(1'b0),
    .C(C_data), .A(A), .B(B));

  // Notes on the sheet:
  //   contents of Addr_A (hex, n*v repeats v):
  //   5 2 7 3 2 0 2 6 2 4 1 3 5 5 2 6
  //   contents of Addr_B (hex, n*v repeats v):
  //   4 4 6 0 2 3 5 5 5 0 0 4 5 3 7 5
  //   contents of Addr_C (hex, n*v repeats v):
  //   0 5 0 5 5 7 2 3 6 4 0 4 7 7 4 6
  //   contents of we (hex, n*v repeats v):
  //   0 0 0 1 0 0 1 0 0 0 1 1 0 0 1 1
  //   contents of C (hex, n*v repeats v):
  //   1 4 c f 0 5 9 7 c b 9 f b 9 1 e
endmodule
